// Digital circuit 4 bit adder modified.dig as structural Verilog
module _4_bit_adder_modified (
  input  [3:0] A,
  input  [3:0] B,
  input  C_in,
  output [3:0] Sum,
  output Ovr
);

  wire full_adder_2_c_out, full_adder_3_c_out, full_adder_4_c_out;

  full_adder full_adder_1 (.A(A[3]), .B(B[3]), .C_in(full_adder_2_c_out), .Sum(Sum[3]), .C_out(Ovr));
  full_adder full_adder_2 (.A(A[2]), .B(B[2]), .C_in(full_adder_3_c_out), .Sum(Sum[2]), .C_out(full_adder_2_c_out));
  full_adder full_adder_3 (.A(A[1]), .B(B[1]), .C_in(full_adder_4_c_out), .Sum(Sum[1]), .C_out(full_adder_3_c_out));
  full_adder full_adder_4 (.A(A[0]), .B(B[0]), .C_in(C_in), .Sum(Sum[0]), .C_out(full_adder_4_c_out));
endmodule
