// Digital circuit 4-bit-processor-updated.dig as structural Verilog
module _4_bit_processor_updated (
  input  Clk,
  input  [1:0] IR_Ctrl,
  input  [3:0] PC_ManLoad,
  input  [1:0] PC_Ctrl,
  input  [1:0] Instruct_Mem_Ctrl,
  input  Instruct_Mem_ChipSelect,
  input  [3:0] Instruct_Mem_Input,
  output [3:0] DataMem_Out,
  output [15:0] Instruct_Out,
  output [3:0] readData1,
  output [3:0] readData2,
  output [3:0] Rout_0,
  output [3:0] Rout_1,
  output [3:0] Rout_2,
  output [3:0] Rout_3
);

  wire instruction_memory_module_updated_1_alu_enable;
  wire [1:0] instruction_decoder_1_a, instruction_decoder_1_b, instruction_decoder_1_register_select;
  wire [2:0] instruction_decoder_1_opcode;
  wire [7:0] instruction_decoder_1_register_ctrl;

  Instruction_Memory_Module_Updated instruction_memory_module_updated_1 (
    .Clk(Clk), .IR_Ctrl(IR_Ctrl), .PC_ManLoad(PC_ManLoad), .PC_Ctrl(PC_Ctrl),
    .Instruct_Mem_Ctrl(Instruct_Mem_Ctrl), .Instruct_Mem_ChipSelect(Instruct_Mem_ChipSelect),
    .Instruct_Mem_Input(Instruct_Mem_Input), .Instruct_Out(Instruct_Out),
    .ALU_Enable(instruction_memory_module_updated_1_alu_enable));
  Instruction_Decoder instruction_decoder_1 (
    .Instruction_Input(Instruct_Out), .ALU_Enable(instruction_memory_module_updated_1_alu_enable),
    .A(instruction_decoder_1_a), .B(instruction_decoder_1_b),
    .Register_Select(instruction_decoder_1_register_select), .OPCODE(instruction_decoder_1_opcode),
    .Register_Ctrl(instruction_decoder_1_register_ctrl));
  Register_File register_file_1 (
    .Select_Read1(instruction_decoder_1_a), .Select_Read2(instruction_decoder_1_b), .Clk(Clk),
    .Write_Data(DataMem_Out), .Write_Register(instruction_decoder_1_register_select),
    .Ctrl_Registers(instruction_decoder_1_register_ctrl), .ReadData_1(readData1), .ReadData_2(readData2),
    .R0_Out(Rout_0), .R1_Out(Rout_1), .R2_Out(Rout_2), .R3_Out(Rout_3));
  ALU alu_1 (
    .A(readData1), .B(readData2), .S_1_S_0_C_in(instruction_decoder_1_opcode), .D_0_Out(DataMem_Out));  // open: D_0_Ovrflw

  // Notes on the sheet:
  //   PC_Ctrl: default 1
endmodule

/* Test case Tests:
Clk Instruct-Mem_ChipSelect Instruct-Mem_Ctrl Instruct-Mem_Input IR_Ctrl readData1 readData2 Instruct_Out DataMem_Out

#INC&ADD

C 1 1 0x0 0 X X X X
C 1 1 0x4 0 X X X X
C 1 1 0x1 0 X X X X
C 1 1 0x0 0 X X X X

C 1 1 0x0 0 X X X X
C 1 1 0x4 0 X X X X
C 1 1 0x1 0 X X X X
C 1 1 0x0 0 X X X X

C 1 1 0x1 0 X X X X
C 1 1 0x5 0 X X X X
C 1 1 0x1 0 X X X X
C 1 1 0x0 0 X X X X

C 1 1 0x2 0 X X X X
C 1 1 0x1 0 X X X X
C 1 1 0x0 0 X X X X
C 1 1 0x0 0 X X X X

C 1 0 0 1 X X X X
C 1 0 0 1 X X X X
C 1 0 0 1 X X X X
C 1 0 0 1 X X X X

C 1 0 0 1 X X X X
C 1 0 0 1 X X X X
C 1 0 0 1 X X X X
C 1 0 0 1 X X X X

C 1 0 0 1 X X X X
C 1 0 0 1 X X X X
C 1 0 0 1 X X X X
C 1 0 0 1 X X X X

C 1 0 0 1 X X X X
C 1 0 0 1 X X X X
C 1 0 0 1 X X X X
C 1 0 0 1 X X X X

#INC&SUB

C 1 1 0x0 0 X X X X
C 1 1 0x4 0 X X X X
C 1 1 0x1 0 X X X X
C 1 1 0x0 0 X X X X

C 1 1 0x0 0 X X X X
C 1 1 0x4 0 X X X X
C 1 1 0x1 0 X X X X
C 1 1 0x0 0 X X X X

C 1 1 0x1 0 X X X X
C 1 1 0x5 0 X X X X
C 1 1 0x1 0 X X X X
C 1 1 0x0 0 X X X X

C 1 1 0x7 0 X X X X
C 1 1 1100 0 X X X X
C 1 1 0x0 0 X X X X
C 1 1 0x0 0 X X X X

C 1 0 0 1 X X X X
C 1 0 0 1 X X X X
C 1 0 0 1 X X X X
C 1 0 0 1 X X X X

C 1 0 0 1 X X X X
C 1 0 0 1 X X X X
C 1 0 0 1 X X X X
C 1 0 0 1 X X X X

C 1 0 0 1 X X X X
C 1 0 0 1 X X X X
C 1 0 0 1 X X X X
C 1 0 0 1 X X X X

C 1 0 0 1 X X X X
C 1 0 0 1 X X X X
C 1 0 0 1 X X X X
C 1 0 0 1 X X X X

#DEC&ADD

C 1 1 0x0 0 X X X X
C 1 1 0x8 0 X X X X
C 1 1 0x1 0 X X X X
C 1 1 0x0 0 X X X X

C 1 1 0x0 0 X X X X
C 1 1 0x8 0 X X X X
C 1 1 0x1 0 X X X X
C 1 1 0x0 0 X X X X

C 1 1 0x0 0 X X X X
C 1 1 0x8 0 X X X X
C 1 1 0x1 0 X X X X
C 1 1 0x0 0 X X X X

C 1 1 0x2 0 X X X X
C 1 1 0x1 0 X X X X
C 1 1 0x0 0 X X X X
C 1 1 0x0 0 X X X X

C 1 0 0 1 X X X X
C 1 0 0 1 X X X X
C 1 0 0 1 X X X X
C 1 0 0 1 X X X X

C 1 0 0 1 X X X X
C 1 0 0 1 X X X X
C 1 0 0 1 X X X X
C 1 0 0 1 X X X X

C 1 0 0 1 X X X X
C 1 0 0 1 X X X X
C 1 0 0 1 X X X X
C 1 0 0 1 X X X X

C 1 0 0 1 X X X X
C 1 0 0 1 X X X X
C 1 0 0 1 X X X X
C 1 0 0 1 X X X X
*/
