// Digital circuit Extended-Instruction-Registers.dig as structural Verilog
module Extended_Instruction_Registers (
  input  Clk,
  input  [1:0] IR_Ctrl,
  input  [3:0] Memory_Input,
  input  [3:0] PC_Input,
  output [15:0] IR_Output,
  output Enable_ALU
);

  wire [1:0] demultiplexer_1_out_0, demultiplexer_1_out_1, demultiplexer_1_out_2, demultiplexer_1_out_3;
  wire [3:0] demultiplexer_2_out_0, demultiplexer_2_out_1, demultiplexer_2_out_2, demultiplexer_2_out_3,
       ir_1_output, ir_2_output, ir_3_output, ir_4_output;

  Demultiplexer #(.Selector_Bits(2), .Bits(2)) demultiplexer_1 (
    .sel(PC_Input[1:0]), .in(IR_Ctrl), .out_0(demultiplexer_1_out_0), .out_1(demultiplexer_1_out_1),
    .out_2(demultiplexer_1_out_2), .out_3(demultiplexer_1_out_3));
  Demultiplexer #(.Selector_Bits(2), .Bits(4)) demultiplexer_2 (
    .sel(PC_Input[1:0]), .in(Memory_Input), .out_0(demultiplexer_2_out_0), .out_1(demultiplexer_2_out_1),
    .out_2(demultiplexer_2_out_2), .out_3(demultiplexer_2_out_3));
  and and_1 (Enable_ALU, ~PC_Input[0], ~PC_Input[1]);  // And
  IR ir_1 (
    .Ctrl__0_Read_1_Write_2_Reset(demultiplexer_1_out_0), .Clock(Clk), .Input(demultiplexer_2_out_0),
    .Output(ir_1_output));
  IR ir_2 (
    .Ctrl__0_Read_1_Write_2_Reset(demultiplexer_1_out_1), .Clock(Clk), .Input(demultiplexer_2_out_1),
    .Output(ir_2_output));
  IR ir_3 (
    .Ctrl__0_Read_1_Write_2_Reset(demultiplexer_1_out_2), .Clock(Clk), .Input(demultiplexer_2_out_2),
    .Output(ir_3_output));
  IR ir_4 (
    .Ctrl__0_Read_1_Write_2_Reset(demultiplexer_1_out_3), .Clock(Clk), .Input(demultiplexer_2_out_3),
    .Output(ir_4_output));
  assign IR_Output = Enable_ALU ? {ir_4_output, ir_3_output, ir_2_output, ir_1_output} : 16'bz;  // Driver driver_1
endmodule
