// Digital circuit Instruction Decoder.dig as structural Verilog
module Instruction_Decoder (
  input  [15:0] Instruction_Input,
  input  ALU_Enable,
  output [1:0] A,
  output [1:0] B,
  output [1:0] Register_Select,
  output [2:0] OPCODE,
  output [7:0] Register_Ctrl
);

  wire [7:0] registerfile_write_ctrl_1_out;

  RegisterFile_Write_Ctrl registerfile_write_ctrl_1 (.Op3(Instruction_Input[1:0]), .Out(registerfile_write_ctrl_1_out));
  Multiplexer #(.Bits(8)) multiplexer_1 (
    .sel(ALU_Enable), .in_0({8{1'b0}}), .in_1(registerfile_write_ctrl_1_out), .out(Register_Ctrl));

  assign A = Instruction_Input[5:4];
  assign B = Instruction_Input[3:2];
  assign OPCODE = Instruction_Input[8:6];
  assign Register_Select = Instruction_Input[1:0];
endmodule
