// Digital circuit Instruction-Memory-Module-Updated.dig as structural Verilog
module Instruction_Memory_Module_Updated (
  input  Clk,
  input  [1:0] IR_Ctrl,
  input  [3:0] PC_ManLoad,
  input  [1:0] PC_Ctrl,
  input  [1:0] Instruct_Mem_Ctrl,
  input  Instruct_Mem_ChipSelect,
  input  [3:0] Instruct_Mem_Input,
  output [15:0] Instruct_Out,
  output ALU_Enable
);

  wire [3:0] memory_1_output, pc_1_output;

  PC pc_1 (.Clock(Clk), .Ctrl(PC_Ctrl), .Load_Manual(PC_ManLoad), .Output(pc_1_output));
  Memory memory_1 (
    .Address(pc_1_output), .Clock(Clk), .Input(Instruct_Mem_Input),
    .Ctrl__0_Read_1_Write_2_Reset(Instruct_Mem_Ctrl), .ChipSelect(Instruct_Mem_ChipSelect),
    .Output(memory_1_output));
  Extended_Instruction_Registers extended_instruction_registers_1 (
    .Clk(Clk), .IR_Ctrl(IR_Ctrl), .Memory_Input(memory_1_output), .PC_Input(pc_1_output),
    .IR_Output(Instruct_Out), .Enable_ALU(ALU_Enable));

  // Notes on the sheet:
  //   PC_Ctrl: default 1
endmodule

/* Test case:
Clk Instruct-Mem_ChipSelect Instruct-Mem_Ctrl Instruct-Mem_Input IR_Ctrl PC_Ctrl PC_ManLoad Instruct_Out ALU_Enable
c 1 1 0 0 1 0 x x
c 1 1 1 0 1 0 x x
c 1 1 2 0 1 0 x x
c 1 1 3 0 1 0 x x
c 1 1 4 0 1 0 x x
c 1 1 5 0 1 0 x x
c 1 1 6 0 1 0 x x
c 1 1 7 0 1 0 x x
c 1 1 8 0 1 0 x x
c 1 1 9 0 1 0 x x
c 1 1 10 0 1 0 x x
c 1 1 11 0 1 0 x x
c 1 1 12 0 1 0 x x
c 1 1 13 0 1 0 x x
c 1 1 14 0 1 0 x x
c 1 1 15 0 1 0 x x
c 1 0 0 1 1 0 x x
c 1 0 0 1 1 0 x x
c 1 0 0 1 1 0 x x
c 1 0 0 1 1 0 x x
c 1 0 0 1 1 0 x x
c 1 0 0 1 1 0 x x
c 1 0 0 1 1 0 x x
c 1 0 0 1 1 0 x x
c 1 0 0 1 1 0 x x
c 1 0 0 1 1 0 x x
c 1 0 0 1 1 0 x x
c 1 0 0 1 1 0 x x
c 1 0 0 1 1 0 x x
c 1 0 0 1 1 0 x x
c 1 0 0 1 1 0 x x
c 1 0 0 1 1 0 x x
*/
