// Digital circuit Memory.dig as structural Verilog
module Memory (
  input  [3:0] Address,
  input  Clock,
  input  [3:0] Input,
  input  [1:0] Ctrl__0_Read_1_Write_2_Reset,
  input  ChipSelect,
  output [3:0] Output
);

  wire demultiplexer_1_out_0, demultiplexer_1_out_1, demultiplexer_1_out_2, demultiplexer_1_out_3,
       demultiplexer_1_out_4, demultiplexer_1_out_5, demultiplexer_1_out_6, demultiplexer_1_out_7,
       demultiplexer_1_out_8, demultiplexer_1_out_9, demultiplexer_1_out_10, demultiplexer_1_out_11,
       demultiplexer_1_out_12, demultiplexer_1_out_13, demultiplexer_1_out_14, demultiplexer_1_out_15;
  wire [3:0] driver_1_out, multiplexer_1_out, R_0_output, R_1_output, R_2_output, R_3_output, R_4_output,
       R_5_output, R_6_output, R_7_output, R_8_output, R_9_output, R_10_output, R_11_output, R_12_output,
       R_13_output, R_14_output, R_15_output;

  assign driver_1_out = ChipSelect ? Input : 4'bz;  // Driver driver_1
  Demultiplexer #(.Selector_Bits(4)) demultiplexer_1 (
    .sel(Address), .in(Clock), .out_0(demultiplexer_1_out_0), .out_1(demultiplexer_1_out_1),
    .out_2(demultiplexer_1_out_2), .out_3(demultiplexer_1_out_3), .out_4(demultiplexer_1_out_4),
    .out_5(demultiplexer_1_out_5), .out_6(demultiplexer_1_out_6), .out_7(demultiplexer_1_out_7),
    .out_8(demultiplexer_1_out_8), .out_9(demultiplexer_1_out_9), .out_10(demultiplexer_1_out_10),
    .out_11(demultiplexer_1_out_11), .out_12(demultiplexer_1_out_12), .out_13(demultiplexer_1_out_13),
    .out_14(demultiplexer_1_out_14), .out_15(demultiplexer_1_out_15));
  _4_bit_register R_0 (
    .Clock(demultiplexer_1_out_0), .Input(driver_1_out), .Ctrl(Ctrl__0_Read_1_Write_2_Reset),
    .Output(R_0_output));
  _4_bit_register R_1 (
    .Clock(demultiplexer_1_out_1), .Input(driver_1_out), .Ctrl(Ctrl__0_Read_1_Write_2_Reset),
    .Output(R_1_output));
  _4_bit_register R_2 (
    .Clock(demultiplexer_1_out_2), .Input(driver_1_out), .Ctrl(Ctrl__0_Read_1_Write_2_Reset),
    .Output(R_2_output));
  _4_bit_register R_3 (
    .Clock(demultiplexer_1_out_3), .Input(driver_1_out), .Ctrl(Ctrl__0_Read_1_Write_2_Reset),
    .Output(R_3_output));
  Multiplexer #(.Selector_Bits(4), .Bits(4)) multiplexer_1 (
    .sel(Address), .in_0(R_0_output), .in_1(R_1_output), .in_2(R_2_output), .in_3(R_3_output),
    .in_4(R_4_output), .in_5(R_5_output), .in_6(R_6_output), .in_7(R_7_output), .in_8(R_8_output),
    .in_9(R_9_output), .in_10(R_10_output), .in_11(R_11_output), .in_12(R_12_output), .in_13(R_13_output),
    .in_14(R_14_output), .in_15(R_15_output), .out(multiplexer_1_out));
  _4_bit_register R_4 (
    .Clock(demultiplexer_1_out_4), .Input(driver_1_out), .Ctrl(Ctrl__0_Read_1_Write_2_Reset),
    .Output(R_4_output));
  _4_bit_register R_5 (
    .Clock(demultiplexer_1_out_5), .Input(driver_1_out), .Ctrl(Ctrl__0_Read_1_Write_2_Reset),
    .Output(R_5_output));
  _4_bit_register R_6 (
    .Clock(demultiplexer_1_out_6), .Input(driver_1_out), .Ctrl(Ctrl__0_Read_1_Write_2_Reset),
    .Output(R_6_output));
  _4_bit_register R_7 (
    .Clock(demultiplexer_1_out_7), .Input(driver_1_out), .Ctrl(Ctrl__0_Read_1_Write_2_Reset),
    .Output(R_7_output));
  _4_bit_register R_8 (
    .Clock(demultiplexer_1_out_8), .Input(driver_1_out), .Ctrl(Ctrl__0_Read_1_Write_2_Reset),
    .Output(R_8_output));
  _4_bit_register R_9 (
    .Clock(demultiplexer_1_out_9), .Input(driver_1_out), .Ctrl(Ctrl__0_Read_1_Write_2_Reset),
    .Output(R_9_output));
  _4_bit_register R_10 (
    .Clock(demultiplexer_1_out_10), .Input(driver_1_out), .Ctrl(Ctrl__0_Read_1_Write_2_Reset),
    .Output(R_10_output));
  _4_bit_register R_11 (
    .Clock(demultiplexer_1_out_11), .Input(driver_1_out), .Ctrl(Ctrl__0_Read_1_Write_2_Reset),
    .Output(R_11_output));
  _4_bit_register R_12 (
    .Clock(demultiplexer_1_out_12), .Input(driver_1_out), .Ctrl(Ctrl__0_Read_1_Write_2_Reset),
    .Output(R_12_output));
  _4_bit_register R_13 (
    .Clock(demultiplexer_1_out_13), .Input(driver_1_out), .Ctrl(Ctrl__0_Read_1_Write_2_Reset),
    .Output(R_13_output));
  _4_bit_register R_14 (
    .Clock(demultiplexer_1_out_14), .Input(driver_1_out), .Ctrl(Ctrl__0_Read_1_Write_2_Reset),
    .Output(R_14_output));
  _4_bit_register R_15 (
    .Clock(demultiplexer_1_out_15), .Input(driver_1_out), .Ctrl(Ctrl__0_Read_1_Write_2_Reset),
    .Output(R_15_output));
  assign Output = ChipSelect ? multiplexer_1_out : 4'bz;  // Driver driver_2
endmodule
