// Digital circuit RegisterFile_Write_Ctrl.dig as structural Verilog
module RegisterFile_Write_Ctrl (
  input  [1:0] Op3,
  output [7:0] Out
);

  Decoder #(.Selector_Bits(2)) decoder_1 (.sel(Op3), .out_0(Out[0]), .out_1(Out[2]), .out_2(Out[4]), .out_3(Out[6]));

  assign {Out[7], Out[5], Out[3], Out[1]} = 4'b0000;
endmodule
