// Digital circuit Register_File.dig as structural Verilog
module Register_File (
  input  [1:0] Select_Read1,
  input  [1:0] Select_Read2,
  input  Clk,
  input  [3:0] Write_Data,
  input  [1:0] Write_Register,
  input  [7:0] Ctrl_Registers,
  output [3:0] ReadData_1,
  output [3:0] ReadData_2,
  output [3:0] R0_Out,
  output [3:0] R1_Out,
  output [3:0] R2_Out,
  output [3:0] R3_Out
);

  wire [3:0] demultiplexer_1_out_0, demultiplexer_1_out_1, demultiplexer_1_out_2, demultiplexer_1_out_3;

  Demultiplexer #(.Selector_Bits(2), .Bits(4)) demultiplexer_1 (
    .sel(Write_Register), .in(Write_Data), .out_0(demultiplexer_1_out_0), .out_1(demultiplexer_1_out_1),
    .out_2(demultiplexer_1_out_2), .out_3(demultiplexer_1_out_3));
  _4_bit_register R_0 (.Clock(Clk), .Input(demultiplexer_1_out_0), .Ctrl(Ctrl_Registers[1:0]), .Output(R0_Out));
  _4_bit_register R_1 (.Clock(Clk), .Input(demultiplexer_1_out_1), .Ctrl(Ctrl_Registers[3:2]), .Output(R1_Out));
  _4_bit_register R_2 (.Clock(Clk), .Input(demultiplexer_1_out_2), .Ctrl(Ctrl_Registers[5:4]), .Output(R2_Out));
  _4_bit_register R_3 (.Clock(Clk), .Input(demultiplexer_1_out_3), .Ctrl(Ctrl_Registers[7:6]), .Output(R3_Out));
  Multiplexer #(.Selector_Bits(2), .Bits(4)) multiplexer_1 (
    .sel(Select_Read1), .in_0(R0_Out), .in_1(R1_Out), .in_2(R2_Out), .in_3(R3_Out), .out(ReadData_1));
  Multiplexer #(.Selector_Bits(2), .Bits(4)) multiplexer_2 (
    .sel(Select_Read2), .in_0(R0_Out), .in_1(R1_Out), .in_2(R2_Out), .in_3(R3_Out), .out(ReadData_2));
endmodule
